// Logisim project ArchiProc.circ as structural Verilog
module UAL (
  input  [7:0] Rs,
  input  [2:0] ctrUAL,
  input  [7:0] Rt,
  output [3:0] flags,
  output [7:0] res
);

  wire adder_1_cout, OF, or_3_out, subtractor_1_bout;
  wire [2:0] bitselector_1_out;
  wire [7:0] adder_1_out, and_1_out, not_1_out, or_1_out, shifter_1_out, shifter_2_out, subtractor_1_out;

  BitSelector #(.group(3)) bitselector_1 (.in(Rt), .out(bitselector_1_out), .sel(2'b00));
  Adder adder_1 (.a(Rs), .b(Rt), .out(adder_1_out), .cout(adder_1_cout));  // open: cin
  Subtractor subtractor_1 (.a(Rs), .b(Rt), .out(subtractor_1_out), .bout(subtractor_1_bout));  // open: bin
  assign or_1_out = Rs | Rt;  // OR_Gate or_1, 8 bits wide
  assign and_1_out = Rs & Rt;  // AND_Gate and_1, 8 bits wide
  assign not_1_out = ~Rs;  // NOT_Gate not_1, 8 bits wide
  Shifter shifter_1 (.in(Rs), .\dist (bitselector_1_out), .out(shifter_1_out));
  Shifter #(.shift("lr")) shifter_2 (.in(Rs), .\dist (bitselector_1_out), .out(shifter_2_out));
  or or_2 (OF, Rs[7], Rt[7]);
  Multiplexer #(.select(3), .enable("false")) multiplexer_1 (
    .in0(adder_1_cout), .in1(subtractor_1_bout), .in2(1'b0), .in3(1'b0), .in4(1'b0), .in5(1'b0), .in6(1'b0),
    .out(flags[3]), .sel(ctrUAL));  // open: in7
  or or_3 (or_3_out, res[0], res[1], res[2], res[3], res[4], res[5], res[6], flags[1]);
  not not_2 (flags[2], or_3_out);
  Multiplexer #(.select(3), .width(8), .enable("false")) multiplexer_2 (
    .in0(adder_1_out), .in1(subtractor_1_out), .in2(or_1_out), .in3(and_1_out), .in4(not_1_out),
    .in5(shifter_1_out), .in6(shifter_2_out), .out({flags[1], res[6:0]}), .sel(ctrUAL));  // open: in7
  xor xor_1 (flags[0], flags[1], OF);

  assign res[7] = flags[1];

  // Other names for the same wires on the sheet: CF[2:0] = ctrUAL; SF[7:0] = {flags[1], res[6:0]};
  //   ZF[7:0] = {flags[1], res[6:0]}
endmodule

module instDecoder (
  input  [3:0] opcode,
  output isJMP,
  output regWrite,
  output isLoad,
  output [2:0] ctrUAL
);

  wire and_1_out, and_2_out, and_3_out;

  and and_1 (and_1_out, opcode[3], opcode[2]);
  or or_1 (isJMP, and_1_out, and_3_out, and_2_out);
  and and_2 (and_2_out, opcode[3], opcode[1]);
  and and_3 (and_3_out, opcode[3], ~opcode[1], opcode[0]);  // AND_Gate
  not not_1 (regWrite, opcode[3]);
  and and_4 (isLoad, ~opcode[3], opcode[2], opcode[1], opcode[0]);  // AND_Gate

  assign ctrUAL = opcode[2:0];
endmodule
